# Fritzing sketch Sketch (saved by Fritzing 0.9.10b)

parts:
  Composant1 = Arduino Nano (Rev3.0)  # not connected
  M1 = DC Motor [voltage_(max)=6V voltage_(min)=3V]
  D2F1 = D2F-FL Omron Snap Action Limit Switch with Level  # not connected
  D2F2 = D2F-FL Omron Snap Action Limit Switch with Level  # not connected
  L298N1 = L298N DC motor driver
  U1 = ESP8266 WiFi Module [part_number=ESP8266]  # not connected
  M2 = DC Motor [voltage_(max)=6V voltage_(min)=3V]
  J1 = ATX24 Pin Power Supply Connector [package=atx24_right_angle]
  D2F3 = D2F-FL Omron Snap Action Limit Switch with Level  # not connected
  D2F4 = D2F-FL Omron Snap Action Limit Switch with Level  # not connected
  S1 = Round Pushbutton  # not connected
  S2 = Round Pushbutton  # not connected

nets:
  N1: M1.pin_1, L298N1.OUT2
  N2: M1.pin_2, L298N1.OUT1
  N3: L298N1.OUT3, M2.pin_2
  N4: L298N1.OUT4, M2.pin_1
  N5: L298N1.12V, J1.-12V
  GND: L298N1.GND, J1.GND
  5V: L298N1.5V, J1.5V

custom parts:
  D2F-FL Omron Snap Action Limit Switch with Level: Snap action switch with stainless steel lever.
  L298N DC motor driver: 2x DC motor driver with 78M05 positive voltage regulator (7..35 V) L298N: max 46 V, 2 A Set 5 V Enable jumper to enable 5 V regultor (needed for the L298N) and +5 V output at screw terminal or supply external +5 V at screw terminal Set ENA and/or ENB to +5 V to enable motor permanently or supply ENA and/or ENB with PWM signal IN1 and IN2 set rotation directory for motor A (OUT1/OUT2) IN2 and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
  ESP8266 WiFi Module: Generic WiFi Module based on the ESP8266 with onboard PCB antenna and UART communications
